// Logisim project 3Bits V 01.circ as structural Verilog: 2 circuits, main circuit main
module main (
  input  A,
  input  B,
  input  A_2,
  input  B_2,
  input  A_3,
  input  B_3,
  output out_7,
  output out_8,
  output out_9,
  output out_10
);

  wire and_1_out, and_2_out, and_3_out, and_4_out, and_5_out, and_6_out, and_7_out, or_2_out, xor_1_out,
       xor_3_out;

  xor xor_1 (xor_1_out, A, B);
  and and_1 (and_1_out, A, or_2_out);
  and and_2 (and_2_out, B, A);
  and and_3 (and_3_out, or_2_out, B);
  xor xor_2 (out_7, xor_1_out, or_2_out);
  or or_1 (out_10, and_1_out, and_2_out, and_3_out);
  and and_4 (and_4_out, A_2, and_7_out);
  and and_5 (and_5_out, B_2, A_2);
  and and_6 (and_6_out, and_7_out, B_2);
  xor xor_3 (xor_3_out, A_2, B_2);
  xor xor_4 (out_8, xor_3_out, and_7_out);
  or or_2 (or_2_out, and_4_out, and_5_out, and_6_out);
  xor xor_5 (out_9, B_3, A_3);
  and and_7 (and_7_out, A_3, B_3);
endmodule

module Registrador (
  input  in_1,
  input  in_2,
  input  in_3,
  input  in_4,
  input  in_5,
  input  in_6,
  output out_7,
  output out_8,
  output out_9
);

  wire clock_1_out, main_1_out_7, main_1_out_8, main_1_out_9;

  main main_1 (
    .A(in_4), .B(in_1), .A_2(in_5), .B_2(in_2), .A_3(in_6), .B_3(in_3), .out_7(main_1_out_7),
    .out_8(main_1_out_8), .out_9(main_1_out_9));  // open: out_10
  Clock clock_1 (.out(clock_1_out));
  D_Flip_Flop d_ff_1 (.clk(clock_1_out), .D(main_1_out_7), .Q(out_7));  // open: Qn, preset, en, reset
  D_Flip_Flop d_ff_2 (.clk(clock_1_out), .D(main_1_out_8), .Q(out_8));  // open: Qn, preset, en, reset
  D_Flip_Flop d_ff_3 (.clk(clock_1_out), .D(main_1_out_9), .Q(out_9));  // open: Qn, preset, en, reset
endmodule
